# Fritzing sketch HodlBot (saved by Fritzing 0.9.3b)
breadboards: 1

parts:
  Raspberry_Pi1 = Raspberry Pi 2
  S1 = Momentary Switch [package=ksa_sealed_tac_switch]
  Part1 = LCD1602-I2C

nets:
  N1: Raspberry_Pi1.GPIO2, Part1.SDA
  N2: Raspberry_Pi1.GPIO4, Part1.SCL
  GND: Raspberry_Pi1.GND, S1.4, Part1.GND
  N3: Raspberry_Pi1.GPIO14, S1.2
  5V: Raspberry_Pi1.5V, Part1.VCC

custom parts:
  LCD1602-I2C: A standard character display, usually with 2x16 characters. Comes in many colors with LCM1602 IIC attached.
